# Fritzing sketch wiring-diagram (saved by Fritzing 0.9.6b)
breadboards: 1

parts:
  MCU1 = Raspberry Pi Zero
  RHT1 = Humidity and Temperature Sensor RHT03
  R1 = Resistor [tolerance=±5% power=0.25 resistance=220 package=THT]

nets:
  N1: MCU1.pin_1, RHT1.Vcc, R1.Pin_0
  N2: MCU1.pin_6, MCU1.pin_20, RHT1.GND_2
  N3: MCU1.pin_7, RHT1.Data-signal, R1.Pin_1
